# Fritzing sketch Parking-sensor (saved by Fritzing 0.9.3b)
breadboards: 1

parts:
  U1 = NodeMCU V1.0
  Grove1 = Grove OLED 128x96
  US-1 = US-016
  LED1 = LED - 5mm [color="Red (633nm)" package="5 mm [THT]"]
  LED2 = LED - 5mm [color="Yellow (595nm)" package="5 mm [THT]"]
  LED3 = LED - 5mm [color="Green (565nm)" package="5 mm [THT]"]
  J1 = Piezo Speaker

nets:
  N1: U1.D0, J1.pin2
  N2: U1.D1, Grove1.SCL
  N3: U1.D2, Grove1.SDA
  3V3: U1.3V3, Grove1.VCC
  GND: U1.GND, Grove1.GND, US-1.GND, LED1.cathode, LED2.cathode, LED3.cathode, J1.pin1
  N4: U1.D6, US-1.Out
  N5: U1.D7, US-1.Range

custom parts:
  NodeMCU V1.0: ESP8266 based NodeMCU
  US-016: This is a US-016 Distance Sensor with analog output capabilities
